# Fritzing sketch Drive Board Connector HAT (saved by Fritzing 0.9.3b)
circuit board: 8.53cm x 5.65cm
breadboards: 1

parts:
  J2 = single row smd male pin header, 2 pins [form="♂ (male)"]
  J3 = single row smd male pin header, 3 pins [form="♂ (male)"]
  J4 = single row smd male pin header, 3 pins [form="♂ (male)"]
  J6 = single row smd male pin header, 3 pins [form="♂ (male)"]
  J7 = single row smd male pin header, 3 pins [form="♂ (male)"]
  J8 = single row smd male pin header, 3 pins [form="♂ (male)"]
  J1 = double row female pin header, 40 pins [form="♀ (female)"]
  J5 = single row smd male pin header, 3 pins [form="♂ (male)"]

nets:
  N1: J2.pin1, J3.pin3, J4.pin3, J6.pin3, J7.pin3, J8.pin3, J1.pin25, J5.pin3
  N2: J2.pin2, J3.pin2, J4.pin2, J6.pin2, J7.pin2, J8.pin2, J1.pin20, J5.pin2
  N3: J3.pin1, J4.pin1, J1.pin37, J5.pin1
  N4: J6.pin1, J7.pin1, J8.pin1, J1.pin5

notes:
  MAVRIC
  Drive board HAT
  +5V
  gnd
